# Fritzing sketch rocnikovka pokus 1 (saved by Fritzing 1.0.6)
breadboards: 1

parts:
  A2 = NEO-6M GPS Module [part_number=GY-GPS6MV2]
  esp1 = ESP32 DevKitc V4
  SIM800L_BO1 = SIM800L BO
  R1 = Resistor [tolerance=±5% power=0.25W resistance=220 package=THT]
  R2 = Resistor [tolerance=±5% power=0.25W resistance=220 package=THT]
  D1 = Rectifier Diode [part_number=1N4001 package="300 mil [THT]"]
  LED1 = LED - 5mm [color="Yellow (592nm)" current=0.030A package="5 mm [THT]"]
  LED2 = LED - 5mm [color="Green (555nm)" current=30mA package="5 mm [THT]"]

nets:
  N1: A2.GND, esp1.GND#18, SIM800L_BO1.pin_7, LED1.anode
  N2: A2.Tx, esp1.IO16
  N3: A2.Rx, esp1.IO17
  VCC: A2.Vcc, esp1.3V3
  N4: esp1.IO18, SIM800L_BO1.pin_8
  N5: esp1.IO19, SIM800L_BO1.pin_9
  N6: esp1.IO23, R1.Pin_1
  N7: esp1.IO33, R2.Pin_1
  N8: esp1.GND#32, LED2.anode
  N9: SIM800L_BO1.pin_11, D1.cathode
  N10: R1.Pin_0, LED1.cathode
  N11: R2.Pin_0, LED2.cathode

custom parts:
  NEO-6M GPS Module: GY-GPS6MV2 NEO-6M GPS Module Module based on U-blox NEO-6M GPS engine, incorporating regulator for 3.3-5V DC input, MS621FE-compatible rechargeable battery for backup and EEPROM for storing configuration settings. Links: NEO-6 series product information page NEO-6 Datasheet
  ESP32 DevKitc V4: ESP32-DevKitC board with ESP32-WROOM-32 module. ESP32-DevKitC V4 is a small-sized ESP32-based development board produced by Espressif. Most of the pins on the ESP module are broken out to the pin headers on the board. The pins D0, D1, D2, D3, CMD and CLK are used internally for communication between ESP32 and SPI flash memory. They are grouped on both sides near the USB connector. Avoid using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
